# Fritzing sketch Esquemaeletrico (saved by Fritzing 0.9.5d)
perfboards: 1

parts:
  Componente3 = Arduino Uno (Rev3)
  U3 = POT [package=pot_mammoth]
  U4 = POT [package=pot_mammoth]
  Componente4 = InvenSense MPU6050
  Mod2 = ossoyoo-lora-module
  M2 = Niren can bus module [package=THT]

nets:
  N1: Componente3.A0, U3.A
  N2: Componente3.A1, U4.A
  N3: Componente3.A4/SDA, Componente4.SCL
  N4: Componente3.A5/SCL, Componente4.SDA
  N5: Componente3.D10_PWM/SS, M2.pin3
  N6: Componente3.D11_PWM/MOSI, M2.pin5
  N7: Componente3.D12/MISO, M2.pin4
  N8: Componente3.D13/SCK, M2.pin6
  N9: Componente3.D0/RX, Mod2.TXD
  N10: Componente3.D1/TX, Mod2.RXD
  3V3: Componente3.3V3, U3.S, Mod2.VCC
  N11: Componente3.GND, U3.E, U4.E, M2.pin2
  N12: U4.S, Componente4.VCC
  N13: M2.pin8, M2.pin9

custom parts:
  ossoyoo-lora-module: Osoyoo Long Distance wireless transceiver Uart LoRa Module.
  Niren can bus module: Niren can bus module availabe on ebay and others. Pcb view assumes that you unsolder the 7 pin header and resolder it on the bottom of the module to connect to the pcb. The two jumpers and the can bus connector remain on the top of the board and don't appear in pcb view.
